// Logisim project ITC-Summers-Daud Shaikh- 33446.circ as structural Verilog: 27 circuits, main circuit main
module main (
  input  in_1
);

  wire bcd_to_7_segment_decoder_3_p1, binary_to_bcd_converter_1_p2, binary_to_bcd_converter_1_p7,
       buzzer_1_p2, Clock, comparator_1_eq, comparator_2_eq, comparator_3_eq, comparator_4_eq,
       comparator_5_eq, digital_oscilloscope_1_p1, j_k_ff_1_q, j_k_ff_2_q, undriven, undriven_2;
  wire [7:0] counter_1_q;

  Clock clock_1 (.out(Clock));
  Counter #(.max('h10)) counter_1 (.clr(in_1), .clk(Clock), .Q(counter_1_q));  // open: load, up, count, D, carry
  // BCD_to_7_Segment_decoder bcd_to_7_segment_decoder_1: pin names not known
  _7_Segment_Display u_7_segment_display_1 ();  // open: g, f, a, b, e, d, c, dp
  // Binary_to_BCD_converter #(.binvalue(8)) binary_to_bcd_converter_1: pin names not known; wires that end beside it: counter_1_q, binary_to_bcd_converter_1_p2, binary_to_bcd_converter_1_p2, {8{1'b0}}, 8'h2, 8'ha, binary_to_bcd_converter_1_p7
  // BCD_to_7_Segment_decoder bcd_to_7_segment_decoder_2: pin names not known; wires that end beside it: binary_to_bcd_converter_1_p7
  // BCD_to_7_Segment_decoder bcd_to_7_segment_decoder_3: pin names not known; wires that end beside it: bcd_to_7_segment_decoder_3_p1
  _7_Segment_Display u_7_segment_display_2 ();  // open: g, f, a, b, e, d, c, dp
  _7_Segment_Display u_7_segment_display_3 ();  // open: g, f, a, b, e, d, c, dp
  Comparator comparator_1 (.a({8{1'b0}}), .b(counter_1_q), .eq(comparator_1_eq));  // open: gt, lt
  Comparator comparator_2 (.a(8'h2), .b(counter_1_q), .eq(comparator_2_eq));  // open: gt, lt
  Comparator comparator_3 (.a(8'ha), .b(counter_1_q), .eq(comparator_3_eq));  // open: gt, lt
  Comparator comparator_4 (.a(8'h5), .b(counter_1_q), .eq(comparator_4_eq));  // open: gt, lt
  Comparator comparator_5 (.a(8'ha), .b(counter_1_q), .eq(comparator_5_eq));  // open: gt, lt
  LED led_1 (.in(comparator_1_eq));
  J_K_Flip_Flop j_k_ff_1 (
    .J(comparator_2_eq), .K(comparator_3_eq), .clk(undriven), .Q(j_k_ff_1_q));  // open: Qn, preset, reset
  J_K_Flip_Flop j_k_ff_2 (
    .J(comparator_4_eq), .K(comparator_5_eq), .clk(undriven_2), .Q(j_k_ff_2_q));  // open: Qn, preset, reset
  // Buzzer buzzer_1: pin names not known; wires that end beside it: bcd_to_7_segment_decoder_3_p1, buzzer_1_p2, buzzer_1_p2, comparator_1_eq
  // Buzzer buzzer_2: pin names not known; wires that end beside it: 8'ha, j_k_ff_2_q
  // Digital_Oscilloscope digital_oscilloscope_1: pin names not known; wires that end beside it: digital_oscilloscope_1_p1, comparator_1_eq, j_k_ff_1_q, j_k_ff_2_q
  // Buzzer buzzer_3: pin names not known; wires that end beside it: j_k_ff_1_q, j_k_ff_2_q
endmodule

module Half_Adder (
  input  in_1,
  input  in_2,
  output Sum,
  output Carry
);

  xor xor_1 (Sum, in_1, in_2);
  and and_1 (Carry, in_1, in_2);
endmodule

module Full_Adder (
  input  in_1,
  input  in_2,
  input  in_3,
  output Sum_Out,
  output Carry_Out
);

  wire half_adder_1_carry, half_adder_1_sum, half_adder_2_carry;

  Half_Adder half_adder_1 (.in_1(in_2), .in_2(in_3), .Sum(half_adder_1_sum), .Carry(half_adder_1_carry));
  Half_Adder half_adder_2 (.in_1(in_1), .in_2(half_adder_1_sum), .Sum(Sum_Out), .Carry(half_adder_2_carry));
  or or_1 (Carry_Out, half_adder_2_carry, half_adder_1_carry);
endmodule

module FourBit_FullAdder (
  input  C1,
  input  A1,
  input  B1,
  input  A2,
  input  B2,
  input  A3,
  input  B3,
  input  A4,
  input  B4,
  output Output1,
  output Output2,
  output Output3,
  output Sum_Out,
  output Carry_Out
);

  wire full_adder_1_sum_out, full_adder_2_sum_out, full_adder_3_sum_out;

  Full_Adder full_adder_1 (.in_1(C1), .in_2(A1), .in_3(B1), .Sum_Out(full_adder_1_sum_out), .Carry_Out(Output1));
  Full_Adder full_adder_2 (
    .in_1(full_adder_1_sum_out), .in_2(A2), .in_3(B2), .Sum_Out(full_adder_2_sum_out), .Carry_Out(Output2));
  Full_Adder full_adder_3 (
    .in_1(full_adder_2_sum_out), .in_2(A3), .in_3(B3), .Sum_Out(full_adder_3_sum_out), .Carry_Out(Output3));
  Full_Adder full_adder_4 (.in_1(full_adder_3_sum_out), .in_2(A4), .in_3(B4), .Sum_Out(Sum_Out), .Carry_Out(Carry_Out));
endmodule

module TwoToOne_Multiplexer (
  input  SelectLine,
  input  Input1,
  input  Input2,
  output Output1
);

  wire and_1_out, and_2_out, not_1_out;

  not not_1 (not_1_out, SelectLine);
  and and_1 (and_1_out, Input1, SelectLine);
  and and_2 (and_2_out, Input2, not_1_out);
  or or_1 (Output1, and_1_out, and_2_out);
endmodule

module FourToOne_Multiplexer (
  input  Select_Line2,
  input  in_2,
  input  in_3,
  input  in_4,
  input  in_5,
  input  Select_Line,
  output Output1
);

  wire twotoone_multiplexer_1_output1, twotoone_multiplexer_2_output1;

  TwoToOne_Multiplexer twotoone_multiplexer_1 (
    .SelectLine(Select_Line), .Input1(in_2), .Input2(in_3), .Output1(twotoone_multiplexer_1_output1));
  TwoToOne_Multiplexer twotoone_multiplexer_2 (
    .SelectLine(in_4), .Input1(in_5), .Input2(Select_Line), .Output1(twotoone_multiplexer_2_output1));
  TwoToOne_Multiplexer twotoone_multiplexer_3 (
    .SelectLine(Select_Line2), .Input1(twotoone_multiplexer_1_output1),
    .Input2(twotoone_multiplexer_2_output1), .Output1(Output1));
endmodule

module NOR_Gate (
  input  in_1,
  input  in_2,
  output out_3
);

  wire transistor_2_out;

  Transistor #(.\type ("n")) transistor_1 (.in(1'b0), .out(out_3), .gate(in_1));
  Transistor transistor_2 (.in(1'b1), .out(transistor_2_out), .gate(in_1));
  Transistor #(.\type ("n")) transistor_3 (.in(1'b0), .out(out_3), .gate(in_2));
  Transistor transistor_4 (.in(transistor_2_out), .out(out_3), .gate(in_2));
endmodule

module NOT_Gate (
  input  in_1,
  output out_2
);

  Transistor transistor_1 (.in(1'b1), .out(out_2), .gate(in_1));
  Transistor #(.\type ("n")) transistor_2 (.in(1'b0), .out(out_2), .gate(in_1));
endmodule

module NAND_Gate (
  input  in_1,
  input  in_2,
  output out_3
);

  wire transistor_2_out;

  Transistor transistor_1 (.in(1'b1), .out(out_3), .gate(in_1));
  Transistor #(.\type ("n")) transistor_2 (.in(1'b0), .out(transistor_2_out), .gate(in_1));
  Transistor transistor_3 (.in(1'b1), .out(out_3), .gate(in_2));
  Transistor #(.\type ("n")) transistor_4 (.in(transistor_2_out), .out(out_3), .gate(in_2));
endmodule

module OR_Gate (
  input  in_1,
  input  in_2,
  output out_3
);

  wire nor_gate_1_out_3;

  NOR_Gate nor_gate_1 (.in_1(in_1), .in_2(in_2), .out_3(nor_gate_1_out_3));
  NOT_Gate not_gate_1 (.in_1(nor_gate_1_out_3), .out_2(out_3));
endmodule

module AND_Gate (
  input  in_1,
  input  in_2,
  output out_3
);

  wire nand_gate_1_out_3;

  NAND_Gate nand_gate_1 (.in_1(in_1), .in_2(in_2), .out_3(nand_gate_1_out_3));
  NOT_Gate not_gate_1 (.in_1(nand_gate_1_out_3), .out_2(out_3));
endmodule

module XOR_Gate (
  input  in_1,
  input  in_2,
  output out_3
);

  wire and_gate_1_out_3, and_gate_2_out_3, not_1_out, not_2_out;

  not not_1 (not_1_out, in_2);
  not not_2 (not_2_out, in_1);
  AND_Gate and_gate_1 (.in_1(in_1), .in_2(not_1_out), .out_3(and_gate_1_out_3));
  AND_Gate and_gate_2 (.in_1(not_2_out), .in_2(in_2), .out_3(and_gate_2_out_3));
  OR_Gate or_gate_1 (.in_1(and_gate_1_out_3), .in_2(and_gate_2_out_3), .out_3(out_3));
endmodule

module XNOR_Gate (
  input  in_1,
  input  in_2,
  output out_3
);

  wire xor_gate_1_out_3;

  XOR_Gate xor_gate_1 (.in_1(in_1), .in_2(in_2), .out_3(xor_gate_1_out_3));
  NOT_Gate not_gate_1 (.in_1(xor_gate_1_out_3), .out_2(out_3));
endmodule

module MULTI_IN_AND (
  input  in_1,
  input  in_2,
  input  in_3,
  output out_4
);

  wire and_gate_1_out_3;

  AND_Gate and_gate_1 (.in_1(in_1), .in_2(in_2), .out_3(and_gate_1_out_3));
  AND_Gate and_gate_2 (.in_1(and_gate_1_out_3), .in_2(in_3), .out_3(out_4));
endmodule

module MULTI_IN_OR (
  input  in_1,
  input  in_2,
  input  in_3,
  output out_4
);

  wire or_gate_1_out_3;

  OR_Gate or_gate_1 (.in_1(in_1), .in_2(in_2), .out_3(or_gate_1_out_3));
  OR_Gate or_gate_2 (.in_1(or_gate_1_out_3), .in_2(in_3), .out_3(out_4));
endmodule

module HALF_ADDER_TransistorGate (
  input  in_1,
  input  in_2,
  output SUM_OUT,
  output CARRY_OUT
);

  XOR_Gate xor_gate_1 (.in_1(in_1), .in_2(in_2), .out_3(SUM_OUT));
  AND_Gate and_gate_1 (.in_1(in_1), .in_2(in_2), .out_3(CARRY_OUT));
endmodule

module ODD1BIT (
  input  A,
  input  B,
  input  Carry_IN,
  output SUM
);

  wire xor_gate_1_out_3;

  XOR_Gate xor_gate_1 (.in_1(A), .in_2(B), .out_3(xor_gate_1_out_3));
  XOR_Gate xor_gate_2 (.in_1(xor_gate_1_out_3), .in_2(Carry_IN), .out_3(SUM));
endmodule

module MAJ_1_BIT (
  input  in_1,
  input  in_2,
  input  in_3,
  output C_OUT
);

  wire and_gate_1_out_3, and_gate_2_out_3, and_gate_3_out_3, or_gate_1_out_3;

  AND_Gate and_gate_1 (.in_1(in_1), .in_2(in_2), .out_3(and_gate_1_out_3));
  AND_Gate and_gate_2 (.in_1(in_2), .in_2(in_3), .out_3(and_gate_2_out_3));
  AND_Gate and_gate_3 (.in_1(in_3), .in_2(in_1), .out_3(and_gate_3_out_3));
  OR_Gate or_gate_1 (.in_1(and_gate_1_out_3), .in_2(and_gate_2_out_3), .out_3(or_gate_1_out_3));
  OR_Gate or_gate_2 (.in_1(or_gate_1_out_3), .in_2(and_gate_3_out_3), .out_3(C_OUT));
endmodule

module Full_Adder_1_Bit (
  input  A,
  input  B,
  input  Carry_IN,
  output Sum,
  output Carry
);

  ODD1BIT odd1bit_1 (.A(A), .B(B), .Carry_IN(Carry_IN), .SUM(Sum));
  MAJ_1_BIT maj_1_bit_1 (.in_1(A), .in_2(B), .in_3(Carry_IN), .C_OUT(Carry));
endmodule

module FullAdder8_Bit (
  input  A1,
  input  B1,
  input  in_3,
  input  A2,
  input  A3,
  input  B2,
  input  B3,
  input  A4,
  input  B4,
  input  A5,
  input  B5,
  input  A6,
  input  B6,
  input  A7,
  input  B7,
  input  A8,
  input  B8,
  output SUM1,
  output Sum2,
  output Sum3,
  output Sum4,
  output Sum5,
  output Sum6,
  output Sum7,
  output Sum8,
  output Carry_Out
);

  wire full_adder_1_bit_2_carry, full_adder_1_bit_3_carry, full_adder_1_bit_4_carry,
       full_adder_1_bit_5_carry, full_adder_1_bit_6_carry, full_adder_1_bit_7_carry;

  Full_Adder_1_Bit full_adder_1_bit_1 (.A(A1), .B(B1), .Carry_IN(in_3), .Sum(SUM1), .Carry(A2));
  Full_Adder_1_Bit full_adder_1_bit_2 (.A(A2), .B(A2), .Carry_IN(A2), .Sum(Sum2), .Carry(full_adder_1_bit_2_carry));
  Full_Adder_1_Bit full_adder_1_bit_3 (
    .A(A3), .B(B3), .Carry_IN(full_adder_1_bit_2_carry), .Sum(Sum3), .Carry(full_adder_1_bit_3_carry));
  Full_Adder_1_Bit full_adder_1_bit_4 (
    .A(A4), .B(B4), .Carry_IN(full_adder_1_bit_3_carry), .Sum(Sum4), .Carry(full_adder_1_bit_4_carry));
  Full_Adder_1_Bit full_adder_1_bit_5 (
    .A(A5), .B(B5), .Carry_IN(full_adder_1_bit_4_carry), .Sum(Sum5), .Carry(full_adder_1_bit_5_carry));
  Full_Adder_1_Bit full_adder_1_bit_6 (
    .A(A6), .B(B6), .Carry_IN(full_adder_1_bit_5_carry), .Sum(Sum6), .Carry(full_adder_1_bit_6_carry));
  Full_Adder_1_Bit full_adder_1_bit_7 (
    .A(A7), .B(B7), .Carry_IN(full_adder_1_bit_6_carry), .Sum(Sum7), .Carry(full_adder_1_bit_7_carry));
  Full_Adder_1_Bit full_adder_1_bit_8 (
    .A(A8), .B(B8), .Carry_IN(full_adder_1_bit_7_carry), .Sum(Sum8), .Carry(Carry_Out));

  assign B2 = A2;
endmodule

module And_8_Bit (
  input  A1,
  input  B1,
  input  A2,
  input  B2,
  input  A3,
  input  B3,
  input  A4,
  input  B4,
  input  A5,
  input  B5,
  input  A6,
  input  B6,
  input  A7,
  input  B7,
  input  A8,
  input  B8,
  output Sum1,
  output Sum2,
  output Sum3,
  output Sum4,
  output Sum5,
  output Sum6,
  output Sum7,
  output Sum8
);

  AND_Gate and_gate_1 (.in_1(A1), .in_2(B1), .out_3(Sum1));
  AND_Gate and_gate_2 (.in_1(A2), .in_2(B2), .out_3(Sum2));
  AND_Gate and_gate_3 (.in_1(A3), .in_2(B3), .out_3(Sum3));
  AND_Gate and_gate_4 (.in_1(A4), .in_2(B4), .out_3(Sum4));
  AND_Gate and_gate_5 (.in_1(A5), .in_2(B5), .out_3(Sum5));
  AND_Gate and_gate_6 (.in_1(A6), .in_2(B6), .out_3(Sum6));
  AND_Gate and_gate_7 (.in_1(A7), .in_2(B7), .out_3(Sum7));
  AND_Gate and_gate_8 (.in_1(A8), .in_2(B8), .out_3(Sum8));
endmodule

module XOR_8_BIT (
  input  A1,
  input  B1,
  input  A2,
  input  B2,
  input  A3,
  input  B3,
  input  A4,
  input  B4,
  input  A5,
  input  B5,
  input  A6,
  input  B6,
  input  A7,
  input  B7,
  input  A8,
  input  B8,
  output Sum1,
  output Sum2,
  output Sum3,
  output Sum4,
  output Sum5,
  output Sum6,
  output Sum7,
  output Sum8
);

  XOR_Gate xor_gate_1 (.in_1(A1), .in_2(B1), .out_3(Sum1));
  XOR_Gate xor_gate_2 (.in_1(A2), .in_2(B2), .out_3(Sum2));
  XOR_Gate xor_gate_3 (.in_1(A3), .in_2(B3), .out_3(Sum3));
  XOR_Gate xor_gate_4 (.in_1(A4), .in_2(B4), .out_3(Sum4));
  XOR_Gate xor_gate_5 (.in_1(A5), .in_2(B5), .out_3(Sum5));
  XOR_Gate xor_gate_6 (.in_1(A6), .in_2(B6), .out_3(Sum6));
  XOR_Gate xor_gate_7 (.in_1(A7), .in_2(B7), .out_3(Sum7));
  XOR_Gate xor_gate_8 (.in_1(A8), .in_2(B8), .out_3(Sum8));
endmodule

module Decoder_3_to_8 (
  input  A1,
  input  A2,
  input  A3,
  output out_4,
  output out_5,
  output out_6,
  output out_7,
  output out_8,
  output out_9,
  output out_10,
  output out_11
);

  wire not_gate_1_out_2, not_gate_2_out_2, not_gate_3_out_2;

  NOT_Gate not_gate_1 (.in_1(A1), .out_2(not_gate_1_out_2));
  NOT_Gate not_gate_2 (.in_1(A2), .out_2(not_gate_2_out_2));
  NOT_Gate not_gate_3 (.in_1(A3), .out_2(not_gate_3_out_2));
  MULTI_IN_AND multi_in_and_1 (.in_1(A1), .in_2(A2), .in_3(A3), .out_4(out_4));
  MULTI_IN_AND multi_in_and_2 (.in_1(not_gate_1_out_2), .in_2(A2), .in_3(A3), .out_4(out_5));
  MULTI_IN_AND multi_in_and_3 (.in_1(A1), .in_2(not_gate_2_out_2), .in_3(A3), .out_4(out_6));
  MULTI_IN_AND multi_in_and_4 (.in_1(not_gate_1_out_2), .in_2(not_gate_2_out_2), .in_3(A3), .out_4(out_7));
  MULTI_IN_AND multi_in_and_5 (.in_1(A1), .in_2(A2), .in_3(not_gate_3_out_2), .out_4(out_8));
  MULTI_IN_AND multi_in_and_6 (.in_1(not_gate_1_out_2), .in_2(A2), .in_3(not_gate_3_out_2), .out_4(out_9));
  MULTI_IN_AND multi_in_and_7 (.in_1(A1), .in_2(not_gate_2_out_2), .in_3(not_gate_3_out_2), .out_4(out_10));
  MULTI_IN_AND multi_in_and_8 (
    .in_1(not_gate_1_out_2), .in_2(not_gate_2_out_2), .in_3(not_gate_3_out_2), .out_4(out_11));
endmodule

module Demux_3_to_8 (
  input  in_1,
  input  in_2,
  input  in_3,
  input  in_4,
  output out_5,
  output out_6,
  output out_7,
  output out_8,
  output out_9,
  output out_10,
  output out_11,
  output out_12
);

  wire decoder_3_to_8_1_out_4, decoder_3_to_8_1_out_5, decoder_3_to_8_1_out_6, decoder_3_to_8_1_out_8,
       decoder_3_to_8_1_out_9, decoder_3_to_8_1_out_10, decoder_3_to_8_1_out_11;

  Decoder_3_to_8 decoder_3_to_8_1 (
    .A1(in_2), .A2(in_3), .A3(in_4), .out_4(decoder_3_to_8_1_out_4), .out_5(decoder_3_to_8_1_out_5),
    .out_6(decoder_3_to_8_1_out_6), .out_7(in_1), .out_8(decoder_3_to_8_1_out_8),
    .out_9(decoder_3_to_8_1_out_9), .out_10(decoder_3_to_8_1_out_10), .out_11(decoder_3_to_8_1_out_11));
  AND_Gate and_gate_1 (.in_1(in_1), .in_2(decoder_3_to_8_1_out_4), .out_3(out_5));
  AND_Gate and_gate_2 (.in_1(in_1), .in_2(decoder_3_to_8_1_out_5), .out_3(out_6));
  AND_Gate and_gate_3 (.in_1(in_1), .in_2(decoder_3_to_8_1_out_6), .out_3(out_7));
  AND_Gate and_gate_4 (.in_1(in_1), .in_2(in_1), .out_3(out_8));
  AND_Gate and_gate_5 (.in_1(in_1), .in_2(decoder_3_to_8_1_out_8), .out_3(out_9));
  AND_Gate and_gate_6 (.in_1(in_1), .in_2(decoder_3_to_8_1_out_9), .out_3(out_10));
  AND_Gate and_gate_7 (.in_1(in_1), .in_2(decoder_3_to_8_1_out_10), .out_3(out_11));
  AND_Gate and_gate_8 (.in_1(in_1), .in_2(decoder_3_to_8_1_out_11), .out_3(out_12));
endmodule

module Decoder_DeMux_3_to_8 (
  input  InputX,
  input  A1,
  input  A2,
  input  A3,
  output Out1,
  output out_6,
  output Out2,
  output Out4,
  output Out3,
  output out_10,
  output Out5,
  output out_12,
  output Out6,
  output Out7,
  output out_15,
  output Out8,
  output out_17,
  output out_18,
  output out_19,
  output out_20
);

  Decoder_3_to_8 decoder_3_to_8_1 (
    .A1(A1), .A2(A2), .A3(A3), .out_4(InputX), .out_5(Out2), .out_6(Out3), .out_7(Out4), .out_8(Out5),
    .out_9(Out6), .out_10(Out7), .out_11(Out8));
  AND_Gate and_gate_1 (.in_1(Out8), .in_2(InputX), .out_3(out_20));
  AND_Gate and_gate_2 (.in_1(InputX), .in_2(InputX), .out_3(out_6));
  AND_Gate and_gate_3 (.in_1(Out2), .in_2(InputX), .out_3(out_10));
  AND_Gate and_gate_4 (.in_1(Out3), .in_2(InputX), .out_3(out_12));
  AND_Gate and_gate_5 (.in_1(Out4), .in_2(InputX), .out_3(out_15));
  AND_Gate and_gate_6 (.in_1(Out5), .in_2(InputX), .out_3(out_17));
  AND_Gate and_gate_7 (.in_1(Out6), .in_2(InputX), .out_3(out_18));
  AND_Gate and_gate_8 (.in_1(Out7), .in_2(InputX), .out_3(out_19));

  assign Out1 = InputX;
endmodule

module OneBit_OneHot_Mux (
  input  ADD_BIT,
  input  ADD_SELECT,
  input  AND_BIT,
  input  AND_SELECT,
  input  XOR_BIT,
  input  XOR_SELECT,
  output HOT_OUT
);

  wire and_gate_1_out_3, and_gate_2_out_3, and_gate_3_out_3;

  AND_Gate and_gate_1 (.in_1(AND_BIT), .in_2(AND_SELECT), .out_3(and_gate_1_out_3));
  AND_Gate and_gate_2 (.in_1(XOR_BIT), .in_2(XOR_SELECT), .out_3(and_gate_2_out_3));
  AND_Gate and_gate_3 (.in_1(ADD_BIT), .in_2(ADD_SELECT), .out_3(and_gate_3_out_3));
  MULTI_IN_OR multi_in_or_1 (
    .in_1(and_gate_3_out_3), .in_2(and_gate_1_out_3), .in_3(and_gate_2_out_3), .out_4(HOT_OUT));
endmodule

module Arithmetic_Logic_Unit (
  input  [7:0] in_1,
  input  [7:0] in_2,
  input  ADD_SELECT,
  input  AND_SELECT,
  input  XOR_SELECT,
  output [7:0] out_6,
  output Carry_Out
);

  wire and_8_bit_1_sum1, and_8_bit_1_sum2, and_8_bit_1_sum3, and_8_bit_1_sum4, and_8_bit_1_sum5,
       and_8_bit_1_sum6, and_8_bit_1_sum7, and_8_bit_1_sum8, fulladder8_bit_1_sum1, fulladder8_bit_1_sum2,
       fulladder8_bit_1_sum3, fulladder8_bit_1_sum4, fulladder8_bit_1_sum5, fulladder8_bit_1_sum6,
       fulladder8_bit_1_sum7, fulladder8_bit_1_sum8, xor_8_bit_1_sum1, xor_8_bit_1_sum2, xor_8_bit_1_sum3,
       xor_8_bit_1_sum4, xor_8_bit_1_sum5, xor_8_bit_1_sum6, xor_8_bit_1_sum7, xor_8_bit_1_sum8;

  FullAdder8_Bit fulladder8_bit_1 (
    .A1(in_1[0]), .B1(in_2[0]), .in_3(1'b1), .A2(in_1[1]), .A3(in_1[2]), .B2(in_2[1]), .B3(in_2[2]),
    .A4(in_1[3]), .B4(in_2[3]), .A5(in_1[4]), .B5(in_2[4]), .A6(in_1[5]), .B6(in_2[5]), .A7(in_1[6]),
    .B7(in_2[6]), .A8(in_1[7]), .B8(in_2[7]), .SUM1(fulladder8_bit_1_sum1), .Sum2(fulladder8_bit_1_sum2),
    .Sum3(fulladder8_bit_1_sum3), .Sum4(fulladder8_bit_1_sum4), .Sum5(fulladder8_bit_1_sum5),
    .Sum6(fulladder8_bit_1_sum6), .Sum7(fulladder8_bit_1_sum7), .Sum8(fulladder8_bit_1_sum8),
    .Carry_Out(Carry_Out));
  And_8_Bit and_8_bit_1 (
    .A1(in_1[0]), .B1(in_2[0]), .A2(in_1[1]), .B2(in_2[1]), .A3(in_1[2]), .B3(in_2[2]), .A4(in_1[3]),
    .B4(in_2[3]), .A5(in_1[4]), .B5(in_2[4]), .A6(in_1[5]), .B6(in_2[5]), .A7(in_1[6]), .B7(in_2[6]),
    .A8(in_1[7]), .B8(in_2[7]), .Sum1(and_8_bit_1_sum1), .Sum2(and_8_bit_1_sum2), .Sum3(and_8_bit_1_sum3),
    .Sum4(and_8_bit_1_sum4), .Sum5(and_8_bit_1_sum5), .Sum6(and_8_bit_1_sum6), .Sum7(and_8_bit_1_sum7),
    .Sum8(and_8_bit_1_sum8));
  XOR_8_BIT xor_8_bit_1 (
    .A1(in_1[0]), .B1(in_2[0]), .A2(in_1[1]), .B2(in_2[1]), .A3(in_1[2]), .B3(in_2[2]), .A4(in_1[3]),
    .B4(in_2[3]), .A5(in_1[4]), .B5(in_2[4]), .A6(in_1[5]), .B6(in_2[5]), .A7(in_1[6]), .B7(in_2[6]),
    .A8(in_1[7]), .B8(in_2[7]), .Sum1(xor_8_bit_1_sum1), .Sum2(xor_8_bit_1_sum2), .Sum3(xor_8_bit_1_sum3),
    .Sum4(xor_8_bit_1_sum4), .Sum5(xor_8_bit_1_sum5), .Sum6(xor_8_bit_1_sum6), .Sum7(xor_8_bit_1_sum7),
    .Sum8(xor_8_bit_1_sum8));
  OneBit_OneHot_Mux onebit_onehot_mux_1 (
    .ADD_BIT(fulladder8_bit_1_sum3), .ADD_SELECT(ADD_SELECT), .AND_BIT(and_8_bit_1_sum3),
    .AND_SELECT(AND_SELECT), .XOR_BIT(xor_8_bit_1_sum3), .XOR_SELECT(XOR_SELECT), .HOT_OUT(out_6[2]));
  OneBit_OneHot_Mux onebit_onehot_mux_2 (
    .ADD_BIT(fulladder8_bit_1_sum4), .ADD_SELECT(ADD_SELECT), .AND_BIT(and_8_bit_1_sum4),
    .AND_SELECT(AND_SELECT), .XOR_BIT(xor_8_bit_1_sum4), .XOR_SELECT(XOR_SELECT), .HOT_OUT(out_6[3]));
  OneBit_OneHot_Mux onebit_onehot_mux_3 (
    .ADD_BIT(fulladder8_bit_1_sum1), .ADD_SELECT(ADD_SELECT), .AND_BIT(and_8_bit_1_sum1),
    .AND_SELECT(AND_SELECT), .XOR_BIT(xor_8_bit_1_sum1), .XOR_SELECT(XOR_SELECT), .HOT_OUT(out_6[0]));
  OneBit_OneHot_Mux onebit_onehot_mux_4 (
    .ADD_BIT(fulladder8_bit_1_sum5), .ADD_SELECT(ADD_SELECT), .AND_BIT(and_8_bit_1_sum5),
    .AND_SELECT(AND_SELECT), .XOR_BIT(xor_8_bit_1_sum5), .XOR_SELECT(XOR_SELECT), .HOT_OUT(out_6[4]));
  OneBit_OneHot_Mux onebit_onehot_mux_5 (
    .ADD_BIT(fulladder8_bit_1_sum6), .ADD_SELECT(ADD_SELECT), .AND_BIT(and_8_bit_1_sum6),
    .AND_SELECT(AND_SELECT), .XOR_BIT(xor_8_bit_1_sum6), .XOR_SELECT(XOR_SELECT), .HOT_OUT(out_6[5]));
  OneBit_OneHot_Mux onebit_onehot_mux_6 (
    .ADD_BIT(fulladder8_bit_1_sum2), .ADD_SELECT(ADD_SELECT), .AND_BIT(and_8_bit_1_sum2),
    .AND_SELECT(AND_SELECT), .XOR_BIT(xor_8_bit_1_sum2), .XOR_SELECT(XOR_SELECT), .HOT_OUT(out_6[1]));
  OneBit_OneHot_Mux onebit_onehot_mux_7 (
    .ADD_BIT(fulladder8_bit_1_sum7), .ADD_SELECT(ADD_SELECT), .AND_BIT(and_8_bit_1_sum7),
    .AND_SELECT(AND_SELECT), .XOR_BIT(xor_8_bit_1_sum7), .XOR_SELECT(XOR_SELECT), .HOT_OUT(out_6[6]));
  OneBit_OneHot_Mux onebit_onehot_mux_8 (
    .ADD_BIT(fulladder8_bit_1_sum8), .ADD_SELECT(ADD_SELECT), .AND_BIT(and_8_bit_1_sum8),
    .AND_SELECT(AND_SELECT), .XOR_BIT(xor_8_bit_1_sum8), .XOR_SELECT(XOR_SELECT), .HOT_OUT(out_6[7]));
endmodule
